# Fritzing sketch segment (saved by Fritzing 0.9.4)
breadboards: 1

parts:
  U1 = 7-SEGMENT-DISPLAY [package=7-segment-display]
  Part1 = Arduino Uno (Rev3)
  R1 = Resistor [tolerance=±5% resistance=330 package=THT]
  R2 = Resistor [tolerance=±5% resistance=330 package=THT]
  R3 = Resistor [tolerance=±5% resistance=330 package=THT]
  R4 = Resistor [tolerance=±5% resistance=330 package=THT]
  R5 = Resistor [tolerance=±5% resistance=330 package=THT]
  R6 = Resistor [tolerance=±5% resistance=330 package=THT]
  R7 = Resistor [tolerance=±5% resistance=330 package=THT]

nets:
  N1: U1.E, R4.Pin_1
  N2: U1.D, R7.Pin_1
  N3: U1.G1, R5.Pin_1
  N4: U1.C, Part1.GND
  N5: U1.DP, R6.Pin_0
  N6: U1.A, R3.Pin_0
  N7: U1.G2, R1.Pin_0
  N8: U1.G, R2.Pin_1
  N9: Part1.D1/TX, R1.Pin_1
  N10: Part1.D2, R3.Pin_1
  N11: Part1.D3_PWM, R6.Pin_1
  N12: Part1.D4, R5.Pin_0
  N13: Part1.D5_PWM, R7.Pin_0
  N14: Part1.D6_PWM, R2.Pin_0
  N15: Part1.D7, R4.Pin_0
